// Logisim project ANTIGO.circ as structural Verilog: 25 circuits, main circuit main
module main (
);

  wire \memExt_saída_read , \memInstr_saída_oparg , \memInstr_saída_opcode , \memInstr_saída_regjump ,
       multiplexer_1_out, multiplexer_2_out, multiplexer_3_out, multiplexer_4_out, multiplexer_5_out,
       \Pilha_saída_read , Pilha_TOS_Returno_saida_tos, \pilhaFuncoes_saída_pc , \Reg_Pilha_saída_operandos ,
       \Reg_Pilha_saída_write , \reg_TOS_funções_saida , regArg_saida, regComp_saida, regDataReturn_saida,
       \regEnd_saída_para_mem_ext , \regJump_saída_mem_mux , \regMemExt_saída_reg_pilha , \regOp1_saída_mux ,
       \regOp2_saída_mux , \regOverflow_saída_controle , \regPc_saída_mem_mux , \RegTOS_saída_mem_mux ,
       somador_sutrator_saida, \ULA_saída_comparação , \ULA_saída_outula , \ULA_saída_overflow , undriven;

  Reg_Operando_1 regOp1 (
    .\Saída_MUX (\regOp1_saída_mux ), .Entrada_Reg_Pilha(\Reg_Pilha_saída_operandos ));  // open: Entrada_CTL, Entrada_CLK
  Reg_Operando_2 regOp2 (
    .\Saída_MUX (\regOp2_saída_mux ), .Entrada_Reg_Pilha(\Reg_Pilha_saída_operandos ));  // open: Entrada_CTL, Entrada_CLK
  Multiplexer multiplexer_1 (
    .in0(\ULA_saída_outula ), .in1(\pilhaFuncoes_saída_pc ), .out(multiplexer_1_out));  // open: sel, en
  \pilha_Funções  pilhaFuncoes (
    .\Saída_PC (\pilhaFuncoes_saída_pc ), .Entrada_Stack_Pointer(\reg_TOS_funções_saida ),
    .Entrada_PC(\regPc_saída_mem_mux ));  // open: Entrada_Ctrl_Write, clk
  reg_TOS_funcoes \reg_TOS_funções  (
    .Saida(\reg_TOS_funções_saida ), .Entrada(somador_sutrator_saida));  // open: Entrada_CTL, Entrada_CLK
  Multiplexer #(.select(2), .enable("false")) multiplexer_2 (
    .in2(\regJump_saída_mem_mux ), .in3(\regOp1_saída_mux ), .out(multiplexer_2_out));  // open: in0, in1, sel
  Multiplexer #(.select(2), .enable("false")) multiplexer_3 (
    .in0(regArg_saida), .in1(\RegTOS_saída_mem_mux ), .in2(\regPc_saída_mem_mux ), .in3(\regOp2_saída_mux ),
    .out(multiplexer_3_out));  // open: sel
  Reg_PC regPc (
    .\Saída_Mem_Mux (\regPc_saída_mem_mux ), .Reg_OutULA(multiplexer_1_out));  // open: Entrada_CTL, Entrada_CLK
  ULA ULA (
    .\Saída_OutULA (\ULA_saída_outula ), .\Saída_Comparação (\ULA_saída_comparação ),
    .\Saída_Overflow (\ULA_saída_overflow ), .Entrada_MUX_Oper_1(multiplexer_3_out),
    .Entrada_MUX_Oper_2(multiplexer_2_out));  // open: Entrada_Controle
  regOverflow regOverflow (
    .\Saída_controle (\regOverflow_saída_controle ), .Entrada(\ULA_saída_overflow ));  // open: Entrada_CTL, Entrada_CLK
  somador_subtrator somador_sutrator (
    .saida(somador_sutrator_saida), .entrada(\reg_TOS_funções_saida ));  // open: Entrada_Controle
  reg_1_1 regComp (.Saida(regComp_saida), .Entrada(\ULA_saída_comparação ));  // open: Entrada_CTL, Entrada_CLK
  \Memoria_Instruções  memInstr (
    .\Saída_OpArg (\memInstr_saída_oparg ), .\Saída_Opcode (\memInstr_saída_opcode ),
    .\Saída_regJump (\memInstr_saída_regjump ), .Entrada_PC(\regPc_saída_mem_mux ));
  reg_1_1 regArg (.Saida(regArg_saida), .Entrada(\memInstr_saída_regjump ));  // open: Entrada_CTL, Entrada_CLK
  reg_1_1 regInstr (.Entrada(\memInstr_saída_opcode ));  // open: Saida, Entrada_CTL, Entrada_CLK
  regJump regJump (
    .\Saída_Mem_Mux (\regJump_saída_mem_mux ), .entrada_regArg(\memInstr_saída_oparg ),
    .Entrada_regJump(regArg_saida));  // open: Entrada_CTL, Entrada_CLK
  \Reg_Endereço  regEnd (
    .\Saída_para_Mem_Ext (\regEnd_saída_para_mem_ext ), .\Entrada_Endereço (\regJump_saída_mem_mux ));  // open: Entrada_CTL, Entrada_CLK
  Multiplexer #(.select(2)) multiplexer_4 (
    .in0(regArg_saida), .in1(\regMemExt_saída_reg_pilha ), .in2(regDataReturn_saida),
    .in3(\ULA_saída_outula ), .out(multiplexer_4_out));  // open: sel, en
  Reg_Pilha Reg_Pilha (
    .Entrada_READ(\Pilha_saída_read ), .\Saída_WRITE (\Reg_Pilha_saída_write ),
    .\Saída_Operandos (\Reg_Pilha_saída_operandos ), .Entrada_MUX(multiplexer_4_out));  // open: Entrada_CTL_write, Entrada_CTL_saida, Entrada_CLK
  reg_return_data regDataReturn (
    .saida(regDataReturn_saida), .entrada_dado(\Pilha_saída_read ));  // open: Entrada_CTL, Entrada_CLK
  reg_end_Bloco Pilha_TOS_Returno (
    .saida_TOS(Pilha_TOS_Returno_saida_tos), .Entrada_Stack_Pointer(\reg_TOS_funções_saida ),
    .Entrada_TOS(\RegTOS_saída_mem_mux ));  // open: Entrada_Ctrl_Write, clk
  Multiplexer multiplexer_5 (
    .in0(\ULA_saída_outula ), .in1(Pilha_TOS_Returno_saida_tos), .out(multiplexer_5_out));  // open: sel, en
  Memoria_Externa memExt (
    .\Saída_READ (\memExt_saída_read ), .Entrada_Write(undriven),
    .\Entrada_Endereço (\regEnd_saída_para_mem_ext ));  // open: Entrada_CTL, Entrada_CLK
  Pilha_1 Pilha (
    .Entrada_WRITE(\Reg_Pilha_saída_write ), .\Saída_READ (\Pilha_saída_read ),
    .Entrada_Reg_TOS(\RegTOS_saída_mem_mux ));  // open: Entrada_CLK, Entrada_Write_CTRL
  Reg_TOS RegTOS (
    .\Saída_Mem_Mux (\RegTOS_saída_mem_mux ), .Reg_OutULA(multiplexer_5_out));  // open: Entrada_CTL, Entrada_CLK
  Reg_Memoria_Ext regMemExt (
    .Entrada_Reg_Pilha(\Reg_Pilha_saída_operandos ), .\Saída_Reg_Pilha (\regMemExt_saída_reg_pilha ),
    .\Saída_WRITE (\memExt_saída_read ), .Entrada_READ(undriven));  // open: Entrada_CTL_WRITE, Entrada_CTL_READ, Entrada_CLK
endmodule

module ULA (
  input  Entrada_Controle,
  input  Entrada_MUX_Oper_1,
  input  Entrada_MUX_Oper_2,
  output \Saída_OutULA ,
  output \Saída_Comparação ,
  output \Saída_Overflow 
);


  // Notes on the sheet:
  //   Executa: OP2 - OP1
  //   OP2 + OP1
  //   OP2 * OP1
  //   OP2 / OP1
  //   OP2 = OP1
  //   OP2 < OP1
  //   OP2 > OP1
  //   É capaz de:
  //   Unidade Lógica Aritmética
  //   *; +; -; /; <; >; =
endmodule

module \Memoria_Instruções  (
  input  Entrada_PC,
  output \Saída_OpArg ,
  output \Saída_Opcode ,
  output \Saída_regJump 
);
endmodule

module Pilha_1 (
  input  Entrada_CLK,
  input  Entrada_WRITE,
  input  Entrada_Write_CTRL,
  input  Entrada_Reg_TOS,
  output \Saída_READ 
);


  // Notes on the sheet:
  //   No caso de operações aritméticas, irá ler um de cada vez e irá atualizando o topo, receberá o resultado e salvará no novo topo (mesma posição do segundo operando)
  //   Sempre estará lendo o que foi solicitado por último e escrevendo na saída de leitura
  //   Só irá escrever quando for solicitado e no topo da pilha
  //   Sempre que executar uma leitura, o valor é excluído da pilha
  //   Sempre que executar uma escrita, o valor é adicionado no topo da pilha
endmodule

module Reg_TOS (
  input  Entrada_CLK,
  input  Reg_OutULA,
  input  Entrada_CTL,
  output \Saída_Mem_Mux 
);


  // Notes on the sheet:
  //   O TOS será crescente a determinada unidade. Então cada WRITE acrescenta uma unidade TOS e cada READ decrementa uma unidade TOS
  //   Receberá sempre o valor de cálculo da ULA
  //   Após calcular o novo TOS
  //   Antes de qualquer WRITE na Pilha, o TOS deverá ser atualizado e então salvar na posição do novo TOS na pilha
endmodule

module Reg_PC (
  input  Entrada_CLK,
  input  Reg_OutULA,
  input  Entrada_CTL,
  output \Saída_Mem_Mux 
);
endmodule

module Reg_Operando_1 (
  input  Entrada_CLK,
  input  Entrada_Reg_Pilha,
  input  Entrada_CTL,
  output \Saída_MUX 
);
endmodule

module Reg_Operando_2 (
  input  Entrada_CLK,
  input  Entrada_Reg_Pilha,
  input  Entrada_CTL,
  output \Saída_MUX 
);
endmodule

module Reg_OutULA (
  input  Entrada_CLK,
  input  Entrada_ULA,
  input  Entrada_CTL,
  output \Saída_PC_Reg_Pilha 
);
endmodule

module Reg_Pilha (
  input  Entrada_MUX,
  input  Entrada_READ,
  input  Entrada_CTL_write,
  input  Entrada_CTL_saida,
  input  Entrada_CLK,
  output \Saída_Operandos ,
  output \Saída_WRITE 
);


  // Notes on the sheet:
  //   Entrada Mem Instr
  //   Entrada regOutULA
  //   Entrada Mem Ext
  //   Os valores recebidos pelo MUX serão repassados para a saida WRITE
  //   O controle WRITE irá permitir a escrita na saída WRITE
  //   O controle SAIDA irá permitir a escrita na saída operandos
  //   Em um LOAD_FAST, irá receber um valor da Memória Externa e passar para a saída WRITE.
  //   Em um STORE_FAST, usará o valor Saída Operandos para enviar para a memória Externa
  //   Em um LOAD_CONST, Entrada_Mem_Instr receberá uma constante vinda da memória de instruções
  //   Irá receber valores diretamente da memória de instruções e da ULA
  //   Deverá receber no CTL qual será a opção de saída
  //   Os valores recebidos na entrada READ serão repassados para a saída!
endmodule

module Reg_Memoria_Ext (
  input  Entrada_Reg_Pilha,
  input  Entrada_READ,
  input  Entrada_CTL_WRITE,
  input  Entrada_CTL_READ,
  input  Entrada_CLK,
  output \Saída_WRITE ,
  output \Saída_Reg_Pilha 
);


  // Notes on the sheet:
  //   sinal: ctrl_RegMemExt_WRITE
  //   sinal: ctrl_RegMemExt_READ
  //   Recebe da pilha e envia para escrever na memória
  //   Lê da memória e envia para o registrador da pilha para salvar na pilha
endmodule

module Memoria_Externa (
  input  Entrada_CLK,
  input  \Entrada_Endereço ,
  input  Entrada_Write,
  input  Entrada_CTL,
  output \Saída_READ 
);
endmodule

module Reg_OpArg (
  input  Entrada_Mem_Inst,
  input  Entrada_CLK,
  input  Entrada_CTL,
  output \Saída_Controle 
);


  // Notes on the sheet:
  //   Salvará o valor referente a Instrução que está sendo executada atualmente, servirá para situar a máquina de estados
endmodule

module \Reg_Comparação  (
  input  Entrada_ULA,
  input  Entrada_CLK,
  input  Entrada_CTL,
  output \Saída_Controle 
);


  // Notes on the sheet:
  //   Salvará 0 ou 1 dizendo se a operação de comparação foi falsa ou verdadeira.
  //   O local para onde o resultado irá ainda não foi definido, mas acredita-se que seja o controle.
  //   Quando for utilizada POP_..._TRUE ou POP_..._FALSE, o controle utilizará o valor salvo aqui para saber o que fazer
endmodule

module \Reg_Endereço  (
  input  Entrada_CLK,
  input  \Entrada_Endereço ,
  input  Entrada_CTL,
  output \Saída_para_Mem_Ext 
);
endmodule

module Reg_Aux_TOS (
  input  Entrada_CLK,
  input  Reg_TOS,
  input  Entrada_CTL,
  output \Saída_para_operando 
);
endmodule

module reg_Argumento (
  input  Entrada_CLK,
  input  Entrada,
  input  Entrada_CTL,
  output \Saída ,
  output \Saída_controle 
);


  // Notes on the sheet:
  //   O controle deverá receber o valor de regArg e 
  //   utiliza-lo para selecionar o seletor da ULA
  //   Quando a operação for uma comparação, o argumento será o tipo de comparação a ser feita, logo deverá chegar ao controle
endmodule

module regOverflow (
  input  Entrada_CLK,
  input  Entrada,
  input  Entrada_CTL,
  output \Saída_controle 
);
endmodule

module \pilha_Funções  (
  input  Entrada_Ctrl_Write,
  input  clk,
  input  Entrada_PC,
  input  Entrada_Stack_Pointer,
  output \Saída_PC 
);
endmodule

module reg_TOS_funcoes (
  input  Entrada_CLK,
  input  Entrada,
  input  Entrada_CTL,
  output Saida
);
endmodule

module somador_subtrator (
  input  Entrada_Controle,
  input  entrada,
  output saida
);
endmodule

module reg_end_Bloco (
  input  Entrada_Ctrl_Write,
  input  clk,
  input  Entrada_TOS,
  input  Entrada_Stack_Pointer,
  output saida_TOS
);
endmodule

module reg_return_data (
  input  Entrada_CLK,
  input  entrada_dado,
  input  Entrada_CTL,
  output saida
);
endmodule

module regJump (
  input  Entrada_CLK,
  input  entrada_regArg,
  input  Entrada_regJump,
  input  Entrada_CTL,
  output \Saída_Mem_Mux 
);
endmodule

module reg_1_1 (
  input  Entrada_CLK,
  input  Entrada,
  input  Entrada_CTL,
  output Saida
);
endmodule
