// Logisim project new.circ as structural Verilog: 26 circuits, main circuit main
module main (
);

  wire \Comp_Stack_saída_read , regOverflow_q, \ULA_saída_comparação , \ULA_saída_overflow ;
  wire [7:0] \memInstr_saída_oparg , \memInstr_saída_opcode , multiplexer_2_out, multiplexer_3_out,
       ram_1_data, regArg_q, regDataReturn_q, regInstr_q, regOp1_q, regOp2_q, regRead_2_q, regRead_q,
       regWrite_2_q, regWrite_q, \Stack_saída_read , \ULA_saída_outula ;
  wire [11:0] adder_1_out, adder_2_out, adder_3_out, multiplexer_1_out, multiplexer_4_out, regAddr_q,
       \regJump_saída_mem_mux , regPC_q, regTos_q, regTosFuncao_q, \Stack_PC_Return_saída_pc ,
       Stack_Tos_Return_saida_tos;
  wire [15:0] \memInstr_saída_regjump ;

  Register regOp2 (.D(regRead_q), .Q(regOp2_q));  // open: en, clk, clr
  Multiplexer #(.select(2), .width(12)) multiplexer_1 (
    .in0(adder_1_out), .in1(\regJump_saída_mem_mux ), .in3(\Stack_PC_Return_saída_pc ),
    .out(multiplexer_1_out));  // open: in2, sel, en
  Register #(.width(12)) regTosFuncao (.D(adder_2_out), .Q(regTosFuncao_q));  // open: en, clk, clr
  Register regOp1 (.D(regRead_q), .Q(regOp1_q));  // open: en, clk, clr
  Multiplexer #(.width(8)) multiplexer_2 (.in0(regArg_q), .in1(regOp2_q), .out(multiplexer_2_out));  // open: sel, en
  Adder #(.width(12)) adder_1 (.a(12'h1), .b(regPC_q), .out(adder_1_out));  // open: cin, cout
  Register #(.width(12)) regPC (.D(multiplexer_1_out), .Q(regPC_q));  // open: en, clk, clr
  \pilha_Funções  Stack_PC_Return (.\Saída_PC (\Stack_PC_Return_saída_pc ), .TOS(regTosFuncao_q), .Entrada_PC(regPC_q));
  Adder #(.width(12)) adder_2 (.b(regTosFuncao_q), .out(adder_2_out));  // open: a, cin, cout
  ULA ULA (
    .\Saída_OutULA (\ULA_saída_outula ), .\Saída_Comparação (\ULA_saída_comparação ),
    .\Saída_Overflow (\ULA_saída_overflow ), .Entrada_MUX_Oper_1(multiplexer_2_out),
    .Entrada_MUX_Oper_2(regOp1_q));
  Register #(.width(1)) regOverflow (.D(\ULA_saída_overflow ), .Q(regOverflow_q));  // open: en, clk, clr
  Comparison_Stack Comp_Stack (
    .Entrada_WRITE(\ULA_saída_comparação ), .TOS(regTos_q), .\Saída_READ (\Comp_Stack_saída_read ));
  \Memoria_Instruções  memInstr (
    .\Saída_regJump (\memInstr_saída_regjump ), .\Saída_OpArg (\memInstr_saída_oparg ),
    .\Saída_Opcode (\memInstr_saída_opcode ), .Entrada_PC(regPC_q));
  reg_end_Bloco Stack_Tos_Return (
    .saida_TOS(Stack_Tos_Return_saida_tos), .Entrada_Stack_Pointer(regTosFuncao_q), .Entrada_TOS(regTos_q));  // open: Entrada_Ctrl_Write, clk
  Register regInstr (.D(\memInstr_saída_oparg ), .Q(regInstr_q));  // open: en, clk, clr
  regJump regJump (
    .\Saída_Mem_Mux (\regJump_saída_mem_mux ), .Entrada_regJump(\memInstr_saída_regjump ),
    .entrada_regArg(regArg_q));
  Register regArg (.D(\memInstr_saída_opcode ), .Q(regArg_q));  // open: en, clk, clr
  Multiplexer #(.select(3), .width(8)) multiplexer_3 (
    .in0(\ULA_saída_outula ), .in1(regRead_2_q), .in2(regDataReturn_q), .in3(regArg_q), .in4(regRead_q),
    .out(multiplexer_3_out));  // open: in5, in6, in7, sel, en
  Register regDataReturn (.D(\Stack_saída_read ), .Q(regDataReturn_q));  // open: en, clk, clr
  Multiplexer #(.width(12)) multiplexer_4 (
    .in0(adder_3_out), .in1(Stack_Tos_Return_saida_tos), .out(multiplexer_4_out));  // open: sel, en
  Register #(.width(12)) regAddr (.D(\regJump_saída_mem_mux ), .Q(regAddr_q));  // open: en, clk, clr
  Register regWrite (.D(multiplexer_3_out), .Q(regWrite_q));  // open: en, clk, clr
  Pilha_1 Stack (.Entrada_WRITE(regWrite_q), .TOS(regTos_q), .\Saída_READ (\Stack_saída_read ));
  Register #(.width(12)) regTos (.D(multiplexer_4_out), .Q(regTos_q));  // open: en, clk, clr
  Register regRead (.D(\Stack_saída_read ), .Q(regRead_q));  // open: en, clk, clr
  Adder #(.width(12)) adder_3 (.a(regTos_q), .b(12'h1), .out(adder_3_out));  // open: cin, cout
  Register regRead_2 (.D(ram_1_data), .Q(regRead_2_q));  // open: en, clk, clr
  RAM #(.addrWidth(12), .bus("separate")) ram_1 (
    .addr(regAddr_q), .din(regWrite_2_q), .data(ram_1_data));  // open: str, sel, clk, ld, clr
  Register regWrite_2 (.D(regRead_q), .Q(regWrite_2_q));  // open: en, clk, clr

  // Notes on the sheet:
  //   Control
endmodule

module ULA (
  input  [7:0] Entrada_MUX_Oper_1,
  input  [7:0] Entrada_MUX_Oper_2,
  output [7:0] \Saída_OutULA ,
  output \Saída_Comparação ,
  output \Saída_Overflow 
);


  // Notes on the sheet:
  //   Executa: OP2 - OP1
  //   OP2 + OP1
  //   OP2 * OP1
  //   OP2 / OP1
  //   OP2 = OP1
  //   OP2 < OP1
  //   OP2 > OP1
  //   É capaz de:
  //   Unidade Lógica Aritmética
  //   *; +; -; /; <; >; =
endmodule

module \Memoria_Instruções  (
  input  [11:0] Entrada_PC,
  output [15:0] \Saída_regJump ,
  output [7:0] \Saída_OpArg ,
  output [7:0] \Saída_Opcode 
);
endmodule

module Pilha_1 (
  input  [11:0] TOS,
  input  [7:0] Entrada_WRITE,
  output [7:0] \Saída_READ 
);


  // Notes on the sheet:
  //   No caso de operações aritméticas, irá ler um de cada vez e irá atualizando o topo, receberá o resultado e salvará no novo topo (mesma posição do segundo operando)
  //   Sempre estará lendo o que foi solicitado por último e escrevendo na saída de leitura
  //   Só irá escrever quando for solicitado e no topo da pilha
  //   Sempre que executar uma leitura, o valor é excluído da pilha
  //   Sempre que executar uma escrita, o valor é adicionado no topo da pilha
endmodule

module Reg_TOS (
  input  Entrada_CLK,
  input  Reg_OutULA,
  input  Entrada_CTL,
  output \Saída_Mem_Mux 
);


  // Notes on the sheet:
  //   O TOS será crescente a determinada unidade. Então cada WRITE acrescenta uma unidade TOS e cada READ decrementa uma unidade TOS
  //   Receberá sempre o valor de cálculo da ULA
  //   Após calcular o novo TOS
  //   Antes de qualquer WRITE na Pilha, o TOS deverá ser atualizado e então salvar na posição do novo TOS na pilha
endmodule

module Reg_PC (
  input  Entrada_CLK,
  input  Reg_OutULA,
  input  Entrada_CTL,
  output \Saída_Mem_Mux 
);
endmodule

module Reg_Operando_1 (
  input  Entrada_CLK,
  input  Entrada_Reg_Pilha,
  input  Entrada_CTL,
  output \Saída_MUX 
);
endmodule

module Reg_Operando_2 (
  input  Entrada_CLK,
  input  Entrada_Reg_Pilha,
  input  Entrada_CTL,
  output \Saída_MUX 
);
endmodule

module Reg_OutULA (
  input  Entrada_CLK,
  input  Entrada_ULA,
  input  Entrada_CTL,
  output \Saída_PC_Reg_Pilha 
);
endmodule

module Reg_Pilha (
  input  Entrada_MUX,
  input  Entrada_READ,
  input  Entrada_CTL_write,
  input  Entrada_CTL_saida,
  input  Entrada_CLK,
  output \Saída_Operandos ,
  output \Saída_WRITE 
);


  // Notes on the sheet:
  //   Entrada Mem Instr
  //   Entrada regOutULA
  //   Entrada Mem Ext
  //   Os valores recebidos pelo MUX serão repassados para a saida WRITE
  //   O controle WRITE irá permitir a escrita na saída WRITE
  //   O controle SAIDA irá permitir a escrita na saída operandos
  //   Em um LOAD_FAST, irá receber um valor da Memória Externa e passar para a saída WRITE.
  //   Em um STORE_FAST, usará o valor Saída Operandos para enviar para a memória Externa
  //   Em um LOAD_CONST, Entrada_Mem_Instr receberá uma constante vinda da memória de instruções
  //   Irá receber valores diretamente da memória de instruções e da ULA
  //   Deverá receber no CTL qual será a opção de saída
  //   Os valores recebidos na entrada READ serão repassados para a saída!
endmodule

module Reg_Memoria_Ext (
  input  Entrada_Reg_Pilha,
  input  Entrada_READ,
  input  Entrada_CTL_WRITE,
  input  Entrada_CTL_READ,
  input  Entrada_CLK,
  output \Saída_WRITE ,
  output \Saída_Reg_Pilha 
);


  // Notes on the sheet:
  //   sinal: ctrl_RegMemExt_WRITE
  //   sinal: ctrl_RegMemExt_READ
  //   Recebe da pilha e envia para escrever na memória
  //   Lê da memória e envia para o registrador da pilha para salvar na pilha
endmodule

module Memoria_Externa (
  input  Entrada_CLK,
  input  \Entrada_Endereço ,
  input  Entrada_Write,
  input  Entrada_CTL,
  output \Saída_READ 
);
endmodule

module Reg_OpArg (
  input  Entrada_Mem_Inst,
  input  Entrada_CLK,
  input  Entrada_CTL,
  output \Saída_Controle 
);


  // Notes on the sheet:
  //   Salvará o valor referente a Instrução que está sendo executada atualmente, servirá para situar a máquina de estados
endmodule

module \Reg_Comparação  (
  input  Entrada_ULA,
  input  Entrada_CLK,
  input  Entrada_CTL,
  output \Saída_Controle 
);


  // Notes on the sheet:
  //   Salvará 0 ou 1 dizendo se a operação de comparação foi falsa ou verdadeira.
  //   O local para onde o resultado irá ainda não foi definido, mas acredita-se que seja o controle.
  //   Quando for utilizada POP_..._TRUE ou POP_..._FALSE, o controle utilizará o valor salvo aqui para saber o que fazer
endmodule

module \Reg_Endereço  (
  input  Entrada_CLK,
  input  \Entrada_Endereço ,
  input  Entrada_CTL,
  output \Saída_para_Mem_Ext 
);
endmodule

module Reg_Aux_TOS (
  input  Entrada_CLK,
  input  Reg_TOS,
  input  Entrada_CTL,
  output \Saída_para_operando 
);
endmodule

module reg_Argumento (
  input  Entrada_CLK,
  input  Entrada,
  input  Entrada_CTL,
  output \Saída ,
  output \Saída_controle 
);


  // Notes on the sheet:
  //   O controle deverá receber o valor de regArg e 
  //   utiliza-lo para selecionar o seletor da ULA
  //   Quando a operação for uma comparação, o argumento será o tipo de comparação a ser feita, logo deverá chegar ao controle
endmodule

module regOverflow (
  input  Entrada_CLK,
  input  Entrada,
  input  Entrada_CTL,
  output \Saída_controle 
);
endmodule

module \pilha_Funções  (
  input  [11:0] Entrada_PC,
  output [11:0] \Saída_PC ,
  output [11:0] TOS
);
endmodule

module reg_TOS_funcoes (
  input  Entrada_CLK,
  input  Entrada,
  input  Entrada_CTL,
  output Saida
);
endmodule

module somador_subtrator (
  input  Entrada_Controle,
  input  entrada,
  output saida
);
endmodule

module reg_end_Bloco (
  input  Entrada_Ctrl_Write,
  input  clk,
  input  [11:0] Entrada_TOS,
  input  [11:0] Entrada_Stack_Pointer,
  output [11:0] saida_TOS
);
endmodule

module reg_return_data (
  input  Entrada_CLK,
  input  entrada_dado,
  input  Entrada_CTL,
  output saida
);
endmodule

module regJump (
  input  [15:0] Entrada_regJump,
  input  [7:0] entrada_regArg,
  output [11:0] \Saída_Mem_Mux 
);
endmodule

module reg_1_1 (
  input  Entrada_CLK,
  input  Entrada,
  input  Entrada_CTL,
  output Saida
);
endmodule

module Comparison_Stack (
  input  [11:0] TOS,
  input  Entrada_WRITE,
  output \Saída_READ 
);
endmodule
